# Fritzing sketch sketch (saved by Fritzing 0.7.4b)
breadboards: 1

parts:
  Arduino1 = Arduino
  R1 = Resistor [tolerance=±5% resistance=22k package=THT]
  TRS1 = Audio Jack (TRS) 3.5mm [package="4Ucon 08780 [THT]"]

nets:
  N1: Arduino1.+5V, R1.Pin_1
  N2: Arduino1.GND, TRS1.Ring, TRS1.Tip
  N3: Arduino1.A0, R1.Pin_0, TRS1.Sleeve
